# Fritzing sketch neopixel_ring_ws2812_5v_usb (saved by Fritzing 0.9.3b)

parts:
  Part1 = 12 NeoPixel Ring [part_number=1643]
  U1 = NodeMCU V1.0 [part_number=1]

nets:
  N1: Part1.IN, U1.D5
  VDD: Part1.VDD, U1.3V3
  GND: Part1.GND, U1.GND

custom parts:
  12 NeoPixel Ring: 12 ultra bright smart LED NeoPixels are arranged in a circle with 1.5" (37mm) outer diameter. The rings are 'chainable' - connect the output pin of one to the input pin of another. Use only one microcontroller pin to control as many as you can chain together! Each LED is addressable as the driver chip is inside the LED. Each one has ~18mA constant current drive so the color will be very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
  NodeMCU V1.0: ESP8266 based NodeMCU
