# Fritzing sketch neopixel_strip_string_ws2811_5v_psu (saved by Fritzing 0.9.3b)

parts:
  NEOPIXEL1 = Neopixel Strip -- Black (30/m) [part_number=1376]
  JACK1 = 2.1mm Barrel Jack with Terminal Block
  D1 = Zener Diode [part_number=1N4732A breakdown_voltage=3.6V package="300 mil [THT]"]
  Nodemcu = NodeMCU V1.0 [part_number=nodemcu]

nets:
  GND: NEOPIXEL1.GND, JACK1.NEG, Nodemcu.GND
  N1: NEOPIXEL1.Din, Nodemcu.D5
  N2: NEOPIXEL1.+5V, D1.cathode
  N3: JACK1.POS, D1.anode, Nodemcu.Vin

custom parts:
  Neopixel Strip -- Black (30/m): These NeoPixel strips have 30 digitally-addressable pixel LEDs per meter and are very affordable and are only 12.5 mm wide, 10 mm if you remove the strip from the casing.
  NodeMCU V1.0: ESP8266 based NodeMCU
